// Logisim project ALU.circ as structural Verilog: 1 circuit, main circuit main
module main (
  input  in_1,
  input  in_2,
  input  in_3,
  input  in_4,
  input  in_5,
  input  in_6,
  input  in_7,
  input  in_8,
  input  in_9,
  input  in_10,
  input  in_11,
  input  in_12,
  input  in_13,
  input  in_14,
  input  in_15,
  input  in_16,
  input  in_17,
  input  in_18,
  input  in_19,
  input  in_20,
  input  in_21,
  input  in_22,
  input  in_23,
  input  in_24,
  input  in_25,
  input  in_26
);

  wire and_1_out, and_2_out, and_3_out, and_4_out, and_5_out, and_6_out, and_7_out, and_8_out, and_9_out,
       and_10_out, and_11_out, and_12_out, and_13_out, and_14_out, and_15_out, and_16_out, and_17_out,
       and_18_out, and_19_out, and_20_out, and_34_out, and_35_out, and_36_out, and_37_out, and_38_out,
       and_39_out, and_40_out, and_41_out, and_42_out, and_43_out, and_44_out, and_45_out, and_46_out,
       and_47_out, and_48_out, and_49_out, and_50_out, and_51_out, and_52_out, and_53_out, and_54_out,
       and_55_out, and_56_out, and_57_out, and_58_out, and_59_out, and_60_out, and_61_out, and_62_out,
       and_63_out, and_64_out, and_65_out, and_66_out, and_67_out, and_68_out, and_69_out, and_70_out,
       and_71_out, and_72_out, and_73_out, and_74_out, and_75_out, and_76_out, and_77_out, and_78_out,
       and_79_out, and_80_out, and_81_out, and_82_out, and_83_out, and_84_out, and_85_out, and_86_out,
       and_87_out, and_88_out, and_89_out, and_90_out, and_91_out, and_92_out, and_93_out, and_94_out,
       and_95_out, and_96_out, and_97_out, and_98_out, and_99_out, and_100_out, and_101_out, and_102_out,
       and_103_out, and_104_out, and_105_out, and_106_out, and_107_out, and_108_out, and_109_out,
       and_110_out, and_111_out, and_112_out, and_113_out, and_114_out, and_115_out, and_116_out,
       and_117_out, and_118_out, and_119_out, and_120_out, and_121_out, and_122_out, and_123_out,
       and_124_out, and_125_out, and_126_out, and_127_out, and_128_out, and_129_out, and_130_out,
       and_131_out, and_132_out, and_133_out, and_134_out, and_135_out, and_136_out, and_137_out,
       and_138_out, and_139_out, and_140_out, and_141_out, and_142_out, and_143_out, and_144_out,
       and_145_out, and_146_out, and_147_out, and_148_out, and_149_out, and_150_out, and_151_out,
       and_152_out, and_153_out, and_154_out, and_155_out, and_156_out, button_1_out, d_ff_1_q, d_ff_2_q,
       d_ff_3_q, d_ff_4_q, d_ff_5_q, d_ff_6_q, d_ff_7_q, d_ff_8_q, d_ff_9_q, d_ff_10_q, d_ff_11_q, d_ff_12_q,
       d_ff_13_q, d_ff_14_q, d_ff_15_q, d_ff_16_q, d_ff_17_q, d_ff_18_q, d_ff_19_q, d_ff_20_q, d_ff_21_q,
       d_ff_22_q, d_ff_23_q, d_ff_24_q, d_ff_25_q, d_ff_26_q, d_ff_27_q, d_ff_28_q, d_ff_29_q, d_ff_30_q,
       decoder_1_out0, nand_1_out, nand_2_out, nand_3_out, nand_4_out, nand_5_out, nand_6_out, nand_7_out,
       nand_8_out, nand_9_out, nand_10_out, nand_11_out, nand_12_out, nand_13_out, nand_14_out, nand_15_out,
       nand_16_out, nand_17_out, nand_18_out, nand_19_out, nand_20_out, nand_21_out, not_1_out, not_2_out,
       not_3_out, not_4_out, not_5_out, not_6_out, or_1_out, or_2_out, or_3_out, or_4_out, or_5_out,
       or_6_out, or_7_out, or_8_out, or_9_out, or_10_out, or_11_out, or_12_out, or_13_out, or_14_out,
       or_15_out, or_16_out, or_17_out, or_18_out, or_19_out, or_20_out, or_21_out, or_22_out, or_23_out,
       or_24_out, or_25_out, or_26_out, or_27_out, or_28_out, or_29_out, or_30_out, or_31_out, or_32_out,
       or_33_out, or_34_out, or_35_out, or_36_out, or_37_out, or_38_out, or_39_out, or_40_out, or_41_out,
       or_42_out, or_43_out, or_44_out, or_45_out, or_46_out, or_47_out, or_48_out, or_49_out, or_50_out,
       or_51_out, or_52_out, or_53_out, or_54_out, or_55_out, or_56_out, or_57_out, or_58_out, or_59_out,
       or_60_out, or_61_out, or_62_out, or_63_out, or_64_out, or_65_out, or_66_out, or_67_out, or_68_out,
       or_69_out, or_70_out, or_71_out, or_72_out, or_73_out, or_74_out, or_75_out, or_76_out, or_77_out,
       or_78_out, or_79_out, or_80_out, or_81_out, or_82_out, or_83_out, or_84_out, or_85_out, or_86_out,
       or_87_out, xor_1_out, xor_2_out, xor_3_out, xor_4_out, xor_5_out, xor_6_out, xor_7_out, xor_8_out,
       xor_9_out, xor_10_out, xor_11_out, xor_12_out, xor_13_out, xor_14_out, xor_15_out, xor_16_out;
  wire [3:0] counter_1_q, undriven;

  Button button_1 (.out(button_1_out));
  and and_1 (and_1_out, in_3, in_2, in_1);
  and and_2 (and_2_out, and_3_out, nand_1_out);
  nand nand_1 (nand_1_out, and_3_out, in_3);
  and and_3 (and_3_out, in_1, in_2);
  and and_4 (and_4_out, in_1, nand_3_out);
  and and_5 (and_5_out, and_6_out, nand_2_out);
  nand nand_2 (nand_2_out, and_6_out, in_2);
  nand nand_3 (nand_3_out, in_1, or_1_out);
  or or_1 (or_1_out, in_2, in_3);
  and and_6 (and_6_out, in_1, in_3);
  and and_7 (and_7_out, in_2, nand_4_out);
  and and_8 (and_8_out, and_9_out, nand_5_out);
  nand nand_4 (nand_4_out, in_2, or_2_out);
  nand nand_5 (nand_5_out, and_9_out, in_1);
  or or_2 (or_2_out, in_1, in_3);
  and and_9 (and_9_out, in_2, in_3);
  and and_10 (and_10_out, in_3, nand_6_out);
  nand nand_6 (nand_6_out, in_3, or_3_out);
  or or_3 (or_3_out, in_1, in_2);
  not not_1 (not_1_out, or_4_out);
  or or_4 (or_4_out, in_1, in_2, in_3);
  and and_11 (and_11_out, in_11, in_13);
  or or_5 (or_5_out, in_12, in_13);
  and and_12 (and_12_out, in_12, in_13);
  or or_6 (or_6_out, in_11, in_13);
  or or_7 (or_7_out, in_11, in_12);
  or or_8 (or_8_out, in_11, in_12, in_13);
  and and_13 (and_13_out, in_11, in_12, in_13);
  nand nand_7 (nand_7_out, and_11_out, in_12);
  and and_14 (and_14_out, and_11_out, nand_7_out);
  and and_15 (and_15_out, in_11, nand_8_out);
  nand nand_8 (nand_8_out, in_11, or_5_out);
  nand nand_9 (nand_9_out, and_12_out, in_11);
  and and_16 (and_16_out, and_12_out, nand_9_out);
  nand nand_10 (nand_10_out, in_12, or_6_out);
  and and_17 (and_17_out, in_12, nand_10_out);
  and and_18 (and_18_out, in_13, nand_11_out);
  nand nand_11 (nand_11_out, in_13, or_7_out);
  not not_2 (not_2_out, or_8_out);
  and and_19 (and_19_out, in_8, in_10);
  or or_9 (or_9_out, in_9, in_10);
  and and_20 (and_20_out, in_9, in_10);
  or or_10 (or_10_out, in_8, in_10);
  or or_11 (or_11_out, in_8, in_9);
  not not_3 (not_3_out, or_12_out);
  or or_12 (or_12_out, in_8, in_9, in_10);
  // AND_Gate and_21 has open pins: in0=in_14, in1=decoder_1_out0, out=open
  // AND_Gate and_22 has open pins: in0=decoder_1_out0, in1=in_15, out=open
  // AND_Gate and_23 has open pins: in0=in_16, in1=decoder_1_out0, out=open
  // AND_Gate and_24 has open pins: in0=decoder_1_out0, in1=in_17, out=open
  // AND_Gate and_25 has open pins: in0=in_18, in1=decoder_1_out0, out=open
  // AND_Gate and_26 has open pins: in0=decoder_1_out0, in1=in_19, out=open
  // AND_Gate and_27 has open pins: in0=in_20, in1=decoder_1_out0, out=open
  // AND_Gate and_28 has open pins: in0=decoder_1_out0, in1=in_21, out=open
  // AND_Gate and_29 has open pins: in0=in_22, in1=decoder_1_out0, out=open
  // AND_Gate and_30 has open pins: in0=decoder_1_out0, in1=in_23, out=open
  // AND_Gate and_31 has open pins: in0=in_24, in1=decoder_1_out0, out=open
  // AND_Gate and_32 has open pins: in0=decoder_1_out0, in1=in_25, out=open
  // AND_Gate and_33 has open pins: in0=in_26, in1=decoder_1_out0, out=open
  and and_34 (and_34_out, in_8, in_9, in_10);
  nand nand_12 (nand_12_out, and_19_out, in_9);
  and and_35 (and_35_out, and_19_out, nand_12_out);
  nand nand_13 (nand_13_out, in_8, or_9_out);
  and and_36 (and_36_out, in_8, nand_13_out);
  nand nand_14 (nand_14_out, and_20_out, in_8);
  and and_37 (and_37_out, and_20_out, nand_14_out);
  nand nand_15 (nand_15_out, in_9, or_10_out);
  and and_38 (and_38_out, in_9, nand_15_out);
  nand nand_16 (nand_16_out, in_10, or_11_out);
  and and_39 (and_39_out, in_10, nand_16_out);
  Counter #(.width(4), .max('hf)) counter_1 (
    .D(undriven), .Q(counter_1_q), .clk(button_1_out));  // open: load, count, carry, clr
  Decoder #(.select(4)) decoder_1 (
    .out0(decoder_1_out0), .sel(counter_1_q));  // open: out1, out2, out3, out4, out5, out6, out7, out8, out9, out10, out11, out12, out13, out14, out15, en
  D_Flip_Flop d_ff_1 (.clk(button_1_out), .D(not_6_out), .Q(d_ff_1_q));  // open: Qn, preset, en, reset
  and and_40 (and_40_out, d_ff_1_q, and_1_out);
  D_Flip_Flop d_ff_2 (.clk(button_1_out), .D(and_78_out), .Q(d_ff_2_q));  // open: Qn, preset, en, reset
  and and_41 (and_41_out, d_ff_2_q, and_1_out);
  not not_4 (not_4_out, and_1_out);
  or or_13 (or_13_out, and_40_out, and_42_out);
  or or_14 (or_14_out, and_41_out, and_43_out);
  and and_42 (and_42_out, not_4_out, or_35_out);
  and and_43 (and_43_out, not_4_out, or_36_out);
  and and_44 (and_44_out, or_30_out, and_2_out);
  xor xor_1 (xor_1_out, or_38_out, or_33_out);
  xor xor_2 (xor_2_out, or_37_out, or_32_out);
  xor xor_3 (xor_3_out, or_14_out, or_31_out);
  xor xor_4 (xor_4_out, or_13_out, or_30_out);
  and and_45 (and_45_out, and_2_out, or_31_out);
  and and_46 (and_46_out, or_32_out, and_2_out);
  and and_47 (and_47_out, and_2_out, or_33_out);
  xor xor_5 (xor_5_out, and_7_out, or_33_out);
  and and_48 (and_48_out, xor_5_out, or_38_out);
  xor xor_6 (xor_6_out, and_7_out, or_32_out);
  and and_49 (and_49_out, xor_6_out, or_37_out);
  xor xor_7 (xor_7_out, and_7_out, or_31_out);
  and and_50 (and_50_out, xor_7_out, or_14_out);
  xor xor_8 (xor_8_out, and_7_out, or_30_out);
  and and_51 (and_51_out, in_10, and_10_out);
  and and_52 (and_52_out, in_9, and_10_out);
  and and_53 (and_53_out, in_8, and_10_out);
  and and_54 (and_54_out, in_7, and_10_out);
  Multiplexer #(.select(4)) multiplexer_1 (
    .in1(and_46_out), .in3(and_47_out));  // open: in0, in2, in4, in5, in6, in7, in8, in9, in10, in11, in12, in13, in14, in15, out, sel, en
  or or_15 (or_15_out, or_38_out, or_33_out);
  or or_16 (or_16_out, or_37_out, or_32_out);
  or or_17 (or_17_out, or_14_out, or_31_out);
  or or_18 (or_18_out, or_13_out, or_30_out);
  and and_55 (and_55_out, or_38_out, or_33_out);
  and and_56 (and_56_out, or_37_out, or_32_out);
  and and_57 (and_57_out, or_14_out, or_31_out);
  and and_58 (and_58_out, or_13_out, or_30_out);
  xor xor_9 (xor_9_out, or_38_out, xor_5_out);
  or or_19 (or_19_out, and_59_out, and_48_out);
  and and_59 (and_59_out, xor_9_out, and_7_out);
  xor xor_10 (xor_10_out, or_37_out, xor_6_out);
  or or_20 (or_20_out, and_75_out, and_49_out);
  xor xor_11 (xor_11_out, or_14_out, xor_7_out);
  xor xor_12 (xor_12_out, or_13_out, xor_8_out);
  and and_60 (and_60_out, or_13_out, xor_8_out);
  and and_61 (and_61_out, in_4, in_6);
  or or_21 (or_21_out, in_5, in_6);
  and and_62 (and_62_out, in_5, in_6);
  or or_22 (or_22_out, in_4, in_6);
  or or_23 (or_23_out, in_4, in_5);
  or or_24 (or_24_out, in_4, in_5, in_6);
  and and_63 (and_63_out, or_15_out, and_5_out);
  and and_64 (and_64_out, or_16_out, and_5_out);
  and and_65 (and_65_out, or_17_out, and_5_out);
  and and_66 (and_66_out, or_18_out, and_5_out);
  and and_67 (and_67_out, and_55_out, and_4_out);
  and and_68 (and_68_out, and_56_out, and_4_out);
  and and_69 (and_69_out, and_57_out, and_4_out);
  and and_70 (and_70_out, and_58_out, and_4_out);
  and and_71 (and_71_out, xor_1_out, and_8_out);
  and and_72 (and_72_out, xor_2_out, and_8_out);
  and and_73 (and_73_out, xor_3_out, and_8_out);
  and and_74 (and_74_out, xor_4_out, and_8_out);
  or or_25 (or_25_out, not_1_out, and_7_out);
  xor xor_13 (xor_13_out, and_7_out, xor_9_out);
  xor xor_14 (xor_14_out, or_19_out, xor_10_out);
  and and_75 (and_75_out, xor_10_out, or_19_out);
  and and_76 (and_76_out, xor_11_out, or_20_out);
  or or_26 (or_26_out, and_76_out, and_50_out);
  and and_77 (and_77_out, or_26_out, xor_12_out);
  or or_27 (or_27_out, and_77_out, and_60_out);
  and and_78 (and_78_out, or_27_out, or_25_out);
  and and_79 (and_79_out, in_4, in_5, in_6);
  nand nand_17 (nand_17_out, and_61_out, in_5);
  and and_80 (and_80_out, and_61_out, nand_17_out);
  nand nand_18 (nand_18_out, in_4, or_21_out);
  and and_81 (and_81_out, in_4, nand_18_out);
  and and_82 (and_82_out, and_62_out, nand_19_out);
  nand nand_19 (nand_19_out, and_62_out, in_4);
  and and_83 (and_83_out, in_5, nand_20_out);
  nand nand_20 (nand_20_out, in_5, or_22_out);
  nand nand_21 (nand_21_out, in_6, or_23_out);
  and and_84 (and_84_out, in_6, nand_21_out);
  not not_5 (not_5_out, or_24_out);
  and and_85 (and_85_out, xor_13_out, or_25_out);
  and and_86 (and_86_out, xor_14_out, or_25_out);
  xor xor_15 (xor_15_out, or_20_out, xor_11_out);
  and and_87 (and_87_out, xor_15_out, or_25_out);
  and and_88 (and_88_out, or_25_out, xor_16_out);
  xor xor_16 (xor_16_out, or_26_out, xor_12_out);
  and and_89 (and_89_out, or_39_out, or_34_out, or_29_out, or_28_out);
  not not_6 (not_6_out, and_89_out);
  and and_90 (and_90_out, button_1_out, and_79_out);
  and and_91 (and_91_out, and_80_out, button_1_out);
  and and_92 (and_92_out, button_1_out, and_81_out);
  and and_93 (and_93_out, and_82_out, button_1_out);
  and and_94 (and_94_out, button_1_out, and_83_out);
  and and_95 (and_95_out, and_84_out, button_1_out);
  and and_96 (and_96_out, button_1_out, not_5_out);
  or or_28 (or_28_out, and_54_out, and_88_out, and_74_out, and_70_out, and_66_out);
  or or_29 (or_29_out, and_53_out, and_87_out, and_73_out, and_69_out, and_65_out);
  and and_97 (and_97_out, or_28_out, button_1_out);
  and and_98 (and_98_out, d_ff_6_q, and_13_out);
  and and_99 (and_99_out, d_ff_5_q, and_13_out);
  and and_100 (and_100_out, d_ff_4_q, and_13_out);
  and and_101 (and_101_out, d_ff_3_q, and_13_out);
  or or_30 (or_30_out, and_98_out, or_40_out);
  or or_31 (or_31_out, and_99_out, or_41_out);
  or or_32 (or_32_out, and_100_out, or_42_out);
  or or_33 (or_33_out, and_101_out, or_43_out);
  or or_34 (or_34_out, and_52_out, and_86_out, and_72_out, and_68_out, and_64_out);
  and and_102 (and_102_out, or_29_out, button_1_out);
  and and_103 (and_103_out, or_34_out, button_1_out);
  D_Flip_Flop d_ff_3 (.clk(and_96_out), .D(and_108_out), .Q(d_ff_3_q));  // open: Qn, preset, en, reset
  D_Flip_Flop d_ff_4 (.clk(and_96_out), .D(and_103_out), .Q(d_ff_4_q));  // open: Qn, preset, en, reset
  D_Flip_Flop d_ff_5 (.clk(and_96_out), .D(and_102_out), .Q(d_ff_5_q));  // open: Qn, preset, en, reset
  D_Flip_Flop d_ff_6 (.clk(and_96_out), .D(and_97_out), .Q(d_ff_6_q));  // open: Qn, preset, en, reset
  and and_104 (and_104_out, d_ff_6_q, and_34_out);
  and and_105 (and_105_out, d_ff_5_q, and_34_out);
  and and_106 (and_106_out, d_ff_4_q, and_34_out);
  and and_107 (and_107_out, d_ff_3_q, and_34_out);
  or or_35 (or_35_out, and_104_out, or_44_out);
  or or_36 (or_36_out, and_105_out, or_45_out);
  or or_37 (or_37_out, and_106_out, or_46_out);
  or or_38 (or_38_out, and_107_out, or_47_out);
  or or_39 (or_39_out, and_51_out, and_85_out, and_71_out, and_67_out, and_63_out);
  and and_108 (and_108_out, or_39_out, button_1_out);
  and and_109 (and_109_out, d_ff_10_q, and_14_out);
  and and_110 (and_110_out, d_ff_9_q, and_14_out);
  and and_111 (and_111_out, d_ff_8_q, and_14_out);
  and and_112 (and_112_out, d_ff_7_q, and_14_out);
  or or_40 (or_40_out, and_109_out, or_48_out);
  or or_41 (or_41_out, and_110_out, or_50_out);
  or or_42 (or_42_out, and_111_out, or_51_out);
  or or_43 (or_43_out, and_112_out, or_52_out);
  and and_113 (and_113_out, d_ff_10_q, and_35_out);
  and and_114 (and_114_out, d_ff_9_q, and_35_out);
  and and_115 (and_115_out, d_ff_8_q, and_35_out);
  and and_116 (and_116_out, d_ff_7_q, and_35_out);
  or or_44 (or_44_out, and_113_out, or_49_out);
  or or_45 (or_45_out, and_114_out, or_53_out);
  or or_46 (or_46_out, and_115_out, or_54_out);
  or or_47 (or_47_out, and_116_out, or_55_out);
  D_Flip_Flop d_ff_7 (.clk(and_95_out), .D(and_108_out), .Q(d_ff_7_q));  // open: Qn, preset, en, reset
  D_Flip_Flop d_ff_8 (.clk(and_95_out), .D(and_103_out), .Q(d_ff_8_q));  // open: Qn, preset, en, reset
  D_Flip_Flop d_ff_9 (.clk(and_95_out), .D(and_102_out), .Q(d_ff_9_q));  // open: Qn, preset, en, reset
  D_Flip_Flop d_ff_10 (.clk(and_95_out), .D(and_97_out), .Q(d_ff_10_q));  // open: Qn, preset, en, reset
  or or_48 (or_48_out, and_117_out, or_56_out);
  or or_49 (or_49_out, and_121_out, or_60_out);
  D_Flip_Flop d_ff_11 (.clk(and_94_out), .D(and_108_out), .Q(d_ff_11_q));  // open: Qn, preset, en, reset
  D_Flip_Flop d_ff_12 (.clk(and_94_out), .D(and_103_out), .Q(d_ff_12_q));  // open: Qn, preset, en, reset
  D_Flip_Flop d_ff_13 (.clk(and_94_out), .D(and_102_out), .Q(d_ff_13_q));  // open: Qn, preset, en, reset
  D_Flip_Flop d_ff_14 (.clk(and_94_out), .D(and_97_out), .Q(d_ff_14_q));  // open: Qn, preset, en, reset
  and and_117 (and_117_out, d_ff_14_q, and_15_out);
  and and_118 (and_118_out, d_ff_13_q, and_15_out);
  and and_119 (and_119_out, d_ff_12_q, and_15_out);
  and and_120 (and_120_out, d_ff_11_q, and_15_out);
  or or_50 (or_50_out, and_118_out, or_57_out);
  or or_51 (or_51_out, and_119_out, or_58_out);
  or or_52 (or_52_out, and_120_out, or_59_out);
  and and_121 (and_121_out, d_ff_14_q, and_36_out);
  and and_122 (and_122_out, d_ff_13_q, and_36_out);
  and and_123 (and_123_out, d_ff_12_q, and_36_out);
  and and_124 (and_124_out, d_ff_11_q, and_36_out);
  or or_53 (or_53_out, and_122_out, or_61_out);
  or or_54 (or_54_out, and_123_out, or_62_out);
  or or_55 (or_55_out, and_124_out, or_63_out);
  or or_56 (or_56_out, and_125_out, or_64_out);
  or or_57 (or_57_out, and_126_out, or_65_out);
  or or_58 (or_58_out, and_127_out, or_66_out);
  or or_59 (or_59_out, and_128_out, or_67_out);
  or or_60 (or_60_out, and_129_out, or_68_out);
  or or_61 (or_61_out, and_130_out, or_69_out);
  or or_62 (or_62_out, and_131_out, or_70_out);
  or or_63 (or_63_out, and_132_out, or_71_out);
  D_Flip_Flop d_ff_15 (.clk(and_93_out), .D(and_108_out), .Q(d_ff_15_q));  // open: Qn, preset, en, reset
  D_Flip_Flop d_ff_16 (.clk(and_93_out), .D(and_103_out), .Q(d_ff_16_q));  // open: Qn, preset, en, reset
  D_Flip_Flop d_ff_17 (.clk(and_93_out), .D(and_102_out), .Q(d_ff_17_q));  // open: Qn, preset, en, reset
  D_Flip_Flop d_ff_18 (.clk(and_93_out), .D(and_97_out), .Q(d_ff_18_q));  // open: Qn, preset, en, reset
  and and_125 (and_125_out, d_ff_18_q, and_16_out);
  and and_126 (and_126_out, d_ff_17_q, and_16_out);
  and and_127 (and_127_out, d_ff_16_q, and_16_out);
  and and_128 (and_128_out, d_ff_15_q, and_16_out);
  and and_129 (and_129_out, d_ff_18_q, and_37_out);
  and and_130 (and_130_out, d_ff_17_q, and_37_out);
  and and_131 (and_131_out, d_ff_16_q, and_37_out);
  and and_132 (and_132_out, d_ff_15_q, and_37_out);
  and and_133 (and_133_out, d_ff_22_q, and_17_out);
  and and_134 (and_134_out, d_ff_21_q, and_17_out);
  and and_135 (and_135_out, d_ff_20_q, and_17_out);
  and and_136 (and_136_out, d_ff_19_q, and_17_out);
  or or_64 (or_64_out, and_133_out, or_72_out);
  or or_65 (or_65_out, and_134_out, or_73_out);
  or or_66 (or_66_out, and_135_out, or_74_out);
  or or_67 (or_67_out, and_136_out, or_75_out);
  or or_68 (or_68_out, and_137_out, or_76_out);
  or or_69 (or_69_out, and_138_out, or_77_out);
  or or_70 (or_70_out, and_139_out, or_78_out);
  or or_71 (or_71_out, and_140_out, or_79_out);
  D_Flip_Flop d_ff_19 (.clk(and_92_out), .D(and_108_out), .Q(d_ff_19_q));  // open: Qn, preset, en, reset
  D_Flip_Flop d_ff_20 (.clk(and_92_out), .D(and_103_out), .Q(d_ff_20_q));  // open: Qn, preset, en, reset
  D_Flip_Flop d_ff_21 (.clk(and_92_out), .D(and_102_out), .Q(d_ff_21_q));  // open: Qn, preset, en, reset
  D_Flip_Flop d_ff_22 (.clk(and_92_out), .D(and_97_out), .Q(d_ff_22_q));  // open: Qn, preset, en, reset
  or or_72 (or_72_out, and_141_out, or_80_out);
  and and_137 (and_137_out, d_ff_22_q, and_38_out);
  and and_138 (and_138_out, d_ff_21_q, and_38_out);
  and and_139 (and_139_out, d_ff_20_q, and_38_out);
  and and_140 (and_140_out, d_ff_19_q, and_38_out);
  and and_141 (and_141_out, d_ff_26_q, and_18_out);
  and and_142 (and_142_out, d_ff_25_q, and_18_out);
  and and_143 (and_143_out, d_ff_24_q, and_18_out);
  and and_144 (and_144_out, d_ff_23_q, and_18_out);
  or or_73 (or_73_out, and_142_out, or_81_out);
  or or_74 (or_74_out, and_143_out, or_82_out);
  or or_75 (or_75_out, and_144_out, or_85_out);
  and and_145 (and_145_out, d_ff_26_q, and_39_out);
  and and_146 (and_146_out, d_ff_25_q, and_39_out);
  and and_147 (and_147_out, d_ff_24_q, and_39_out);
  and and_148 (and_148_out, d_ff_23_q, and_39_out);
  or or_76 (or_76_out, and_145_out, or_83_out);
  or or_77 (or_77_out, and_146_out, or_84_out);
  or or_78 (or_78_out, and_147_out, or_86_out);
  or or_79 (or_79_out, and_148_out, or_87_out);
  D_Flip_Flop d_ff_23 (.clk(and_91_out), .D(and_108_out), .Q(d_ff_23_q));  // open: Qn, preset, en, reset
  D_Flip_Flop d_ff_24 (.clk(and_91_out), .D(and_103_out), .Q(d_ff_24_q));  // open: Qn, preset, en, reset
  D_Flip_Flop d_ff_25 (.clk(and_91_out), .D(and_102_out), .Q(d_ff_25_q));  // open: Qn, preset, en, reset
  D_Flip_Flop d_ff_26 (.clk(and_91_out), .D(and_97_out), .Q(d_ff_26_q));  // open: Qn, preset, en, reset
  buf or_80 (or_80_out, and_149_out);  // OR_Gate
  buf or_81 (or_81_out, and_150_out);  // OR_Gate
  buf or_82 (or_82_out, and_151_out);  // OR_Gate
  buf or_83 (or_83_out, and_153_out);  // OR_Gate
  buf or_84 (or_84_out, and_154_out);  // OR_Gate
  D_Flip_Flop d_ff_27 (.clk(and_90_out), .D(and_108_out), .Q(d_ff_27_q));  // open: Qn, preset, en, reset
  D_Flip_Flop d_ff_28 (.clk(and_90_out), .D(and_103_out), .Q(d_ff_28_q));  // open: Qn, preset, en, reset
  D_Flip_Flop d_ff_29 (.clk(and_90_out), .D(and_102_out), .Q(d_ff_29_q));  // open: Qn, preset, en, reset
  D_Flip_Flop d_ff_30 (.clk(and_90_out), .D(and_97_out), .Q(d_ff_30_q));  // open: Qn, preset, en, reset
  and and_149 (and_149_out, d_ff_30_q, not_2_out);
  and and_150 (and_150_out, d_ff_29_q, not_2_out);
  and and_151 (and_151_out, d_ff_28_q, not_2_out);
  and and_152 (and_152_out, d_ff_27_q, not_2_out);
  buf or_85 (or_85_out, and_152_out);  // OR_Gate
  and and_153 (and_153_out, d_ff_30_q, not_3_out);
  and and_154 (and_154_out, d_ff_29_q, not_3_out);
  and and_155 (and_155_out, d_ff_28_q, not_3_out);
  and and_156 (and_156_out, d_ff_27_q, not_3_out);
  buf or_86 (or_86_out, and_155_out);  // OR_Gate
  buf or_87 (or_87_out, and_156_out);  // OR_Gate

  // Notes on the sheet:
  //   Load
  //   +
  //   or
  //   and
  //   xor
  //   -
  //   Overflow
endmodule
