// Logisim project ALU8bits.circ as structural Verilog: 1 circuit, main circuit main
module main (
  input  [7:0] in_1,
  input  [7:0] in_2,
  input  [3:0] in_3,
  input  [1:0] in_4,
  output [7:0] out_5,
  output [3:0] out_6
);

  wire adder_1_cout, decoder_1_out0, decoder_1_out1, decoder_1_out2, decoder_1_out3, decoder_1_out4,
       decoder_1_out5, decoder_1_out6, decoder_1_out7, decoder_1_out8, or_1_out, or_3_out, or_4_out,
       undriven, undriven_2;
  wire [1:0] priority_encoder_2_out;
  wire [2:0] priority_encoder_1_out;
  wire [7:0] adder_1_out, and_1_out, bit_extender_1_out, divider_1_out, divider_1_rem, multiplexer_1_out,
       multiplexer_3_out, multiplier_1_cout, multiplier_1_out, not_1_out, not_2_out, not_3_out, or_2_out,
       xor_1_out;
  wire [7:4] multiplexer_4_out;

  assign not_1_out = ~in_2;  // NOT_Gate not_1, 8 bits wide
  assign not_2_out = ~in_1;  // NOT_Gate not_2, 8 bits wide
  Decoder #(.select(4), .enable("false")) decoder_1 (
    .out0(decoder_1_out0), .out1(decoder_1_out1), .out2(decoder_1_out2), .out3(decoder_1_out3),
    .out4(decoder_1_out4), .out5(decoder_1_out5), .out6(decoder_1_out6), .out7(decoder_1_out7),
    .out8(decoder_1_out8), .sel(in_3));  // open: out9, out10, out11, out12, out13, out14, out15
  Multiplexer #(.width(8)) multiplexer_1 (
    .in0(in_2), .in1(not_1_out), .out(multiplexer_1_out), .sel(decoder_1_out3), .en(or_1_out));
  or or_1 (or_1_out, decoder_1_out2, decoder_1_out3);
  Adder adder_1 (.a(in_1), .b(multiplexer_1_out), .out(adder_1_out), .cin(decoder_1_out3), .cout(adder_1_cout));
  assign and_1_out = in_1 & in_2;  // AND_Gate and_1, 8 bits wide
  assign or_2_out = in_1 | in_2;  // OR_Gate or_2, 8 bits wide
  assign xor_1_out = in_1 ^ in_2;  // XOR_Gate xor_1, 8 bits wide
  Multiplier multiplier_1 (.a(in_1), .b(in_2), .out(multiplier_1_out), .cout(multiplier_1_cout));  // open: cin
  Divider divider_1 (.a(in_1), .b(in_2), .out(divider_1_out), .rem(divider_1_rem));  // open: upper
  Priority_Encoder priority_encoder_1 (
    .in0(or_3_out), .in1(decoder_1_out6), .in2(decoder_1_out7), .in3(decoder_1_out8), .in4(decoder_1_out4),
    .in5(decoder_1_out5), .in6(decoder_1_out0), .out(priority_encoder_1_out));  // open: in7, en_in
  or or_3 (or_3_out, decoder_1_out2, decoder_1_out3);
  assign bit_extender_1_out = {{7{1'b0}}, adder_1_cout};  // Bit_Extender bit_extender_1
  Multiplexer #(.select(3), .width(8)) multiplexer_2 (
    .in0(adder_1_out), .in1(and_1_out), .in2(or_2_out), .in3(xor_1_out), .in4(multiplier_1_out),
    .in5(divider_1_out), .in6(not_2_out), .out(out_5), .sel(priority_encoder_1_out), .en(undriven));  // open: in7
  Multiplexer #(.select(2), .width(8)) multiplexer_3 (
    .in0(bit_extender_1_out), .in1(multiplier_1_cout), .in2(divider_1_rem), .out(multiplexer_3_out),
    .sel(priority_encoder_2_out), .en(undriven_2));  // open: in3
  Priority_Encoder #(.select(2)) priority_encoder_2 (
    .in0(or_4_out), .in1(decoder_1_out4), .in2(decoder_1_out5), .out(priority_encoder_2_out));  // open: in3
  or or_4 (or_4_out, decoder_1_out2, decoder_1_out3);
  assign not_3_out = ~out_5;  // NOT_Gate not_3, 8 bits wide
  Multiplexer #(.select(2), .width(8), .enable("false")) multiplexer_4 (
    .in0(not_3_out), .in1(multiplexer_3_out), .out({multiplexer_4_out, out_6}), .sel(in_4));  // open: in2, in3
endmodule
